# Fritzing sketch Control_Box (saved by Fritzing 1.0.5)
breadboards: 1

parts:
  DS3231_RTC_Module = ZS-042 RTC Module
  24V_Stepper_Motor_Plug = Power plug
  Red/Blue_Stepper_Connections = Power plug
  Green/Black_Stepper_Connections = Power plug
  12V_Linear_Actuator_Plug = Power plug
  Arduino_UNO_R4 = Arduino Uno (Rev3)
  Satellite_Dish = Antenna
  NooElec_SAWbird+_1420_MHz_LNA = IC, DIP package, 4 pins [chip_label=Sawbird]
  RTL-SDR_Blog_V3_R860_RTL2832U = mystery part, 2 pins [chip_label=RTL-SDR]
  L298N_Motor_Driver_Controller = IC, DIP package, 8 pins [chip_label="L298N Driver"]
  I2C_LCD_Screen = IC, DIP package, 4 pins [chip_label=LCD]
  0_96_inch_OLED_Screen = IC, DIP package, 4 pins [chip_label=OLED]
  Stepper_Motor_Driver = IC, DIP package, 12 pins [chip_label="Stepper Driver"]
  Linear_Actuator = mystery part, 2 pins [chip_label=Elevation]
  NEO-6M_GPS_Module = IC, DIP package, 6 pins [chip_label=GPS]
  Elevation_Potentiometer = POT [knob_status=50% power=0.5W package=alps_pot]
  Azimuth_Potentiometer = POT [knob_status=50% power=0.5W package=alps_pot]

nets:
  GND: DS3231_RTC_Module.GND, Arduino_UNO_R4.GND, NooElec_SAWbird+_1420_MHz_LNA.pin3, I2C_LCD_Screen.pin1, 0_96_inch_OLED_Screen.pin2, Elevation_Potentiometer.A, Azimuth_Potentiometer.A
  N1: DS3231_RTC_Module.VCC, L298N_Motor_Driver_Controller.pin4, NEO-6M_GPS_Module.pin1
  N2: DS3231_RTC_Module.SDA, Arduino_UNO_R4.A4/SDA, I2C_LCD_Screen.pin4, 0_96_inch_OLED_Screen.pin3
  N3: DS3231_RTC_Module.SCL, Arduino_UNO_R4.A5/SCL, I2C_LCD_Screen.pin3, 0_96_inch_OLED_Screen.pin4
  N4: 24V_Stepper_Motor_Plug.GND, Stepper_Motor_Driver.pin11
  N5: 24V_Stepper_Motor_Plug.VCC, Stepper_Motor_Driver.pin12
  N6: Red/Blue_Stepper_Connections.GND, Stepper_Motor_Driver.pin7
  N7: Red/Blue_Stepper_Connections.VCC, Stepper_Motor_Driver.pin8
  N8: Green/Black_Stepper_Connections.GND, Stepper_Motor_Driver.pin9
  N9: Green/Black_Stepper_Connections.VCC, Stepper_Motor_Driver.pin10
  N10: 12V_Linear_Actuator_Plug.GND, L298N_Motor_Driver_Controller.pin5
  N11: 12V_Linear_Actuator_Plug.VCC, L298N_Motor_Driver_Controller.pin3
  N12: Arduino_UNO_R4.A0, Azimuth_Potentiometer.S
  N13: Arduino_UNO_R4.A1, Elevation_Potentiometer.S
  N14: Arduino_UNO_R4.D8, NEO-6M_GPS_Module.pin5
  N15: Arduino_UNO_R4.D9_PWM, L298N_Motor_Driver_Controller.pin2
  N16: Arduino_UNO_R4.D0/RX, NEO-6M_GPS_Module.pin3
  N17: Arduino_UNO_R4.D1/TX, NEO-6M_GPS_Module.pin4
  N18: Arduino_UNO_R4.D2, L298N_Motor_Driver_Controller.pin1
  N19: Arduino_UNO_R4.D4, Stepper_Motor_Driver.pin1
  N20: Arduino_UNO_R4.D5_PWM, Stepper_Motor_Driver.pin3
  N21: Arduino_UNO_R4.D6_PWM, Stepper_Motor_Driver.pin5
  N22: Arduino_UNO_R4.5V, NooElec_SAWbird+_1420_MHz_LNA.pin4, I2C_LCD_Screen.pin2, 0_96_inch_OLED_Screen.pin1, Elevation_Potentiometer.E, Azimuth_Potentiometer.E
  N23: Satellite_Dish.antenna_lead, NooElec_SAWbird+_1420_MHz_LNA.pin1
  N24: NooElec_SAWbird+_1420_MHz_LNA.pin2, RTL-SDR_Blog_V3_R860_RTL2832U.pin1
  N25: L298N_Motor_Driver_Controller.pin6, Linear_Actuator.pin2
  N26: L298N_Motor_Driver_Controller.pin7, Linear_Actuator.pin1
  N27: Stepper_Motor_Driver.pin2, Stepper_Motor_Driver.pin4, Stepper_Motor_Driver.pin6, NEO-6M_GPS_Module.pin2

notes:
  GNU Radio
  Radio Telescope, Radio telescope control box wiring for azimuth and elevation motors., 1
  Red: +5v Power
  Black: Ground
  Blue: SDA
  Purple: SCL
  Other Colors: Various Connections
